// Digital circuit 16x8_RAMed.dig as structural Verilog
module _16x8_RAMed (
  input  I1,
  input  I2,
  input  I3,
  input  I4,
  input  I5,
  input  I6,
  input  I7,
  input  I0,
  input  CLK,
  input  S1,
  input  S0,
  input  WR,
  input  S3,
  input  S2,
  input  RD,
  output O0,
  output O1,
  output O2,
  output O3,
  output O4,
  output O5,
  output O6,
  output O7
);

  wire I0_t, I1_t, I2_t, I3_t, I4_t, I5_t, I6_t, I7_t, O00, O01, O02, O03, O10, O11, O12, O13, O20, O21, O22,
       O23, O30, O31, O32, O33, O40, O41, O42, O43, O50, O51, O52, O53, O60, O61, O62, O63, O70, O71, O72,
       O73, RD0, RD1, RD2, RD3, WR0, WR1, WR2, WR3;

  and and_1 (I0_t, I0, WR);
  and and_2 (I1_t, I1, WR);
  and and_3 (I2_t, I2, WR);
  and and_4 (I3_t, I3, WR);
  and and_5 (I4_t, I4, WR);
  and and_6 (I5_t, I5, WR);
  and and_7 (I6_t, I6, WR);
  and and_8 (I7_t, I7, WR);
  _2Bit_Decoder _2bit_decoder_1 (.S0(S2), .S1(S3), .EN(WR), .O0(WR0), .O1(WR1), .O2(WR2), .O3(WR3));
  _4x8Ram _4x8ram_1 (
    .I0(I0_t), .I1(I1_t), .I2(I2_t), .I3(I3_t), .I4(I4_t), .I5(I5_t), .I6(I6_t), .I7(I7_t), .CLK(CLK),
    .S0(S0), .S1(S1), .WR(WR0), .RD(RD0), .O0(O00), .O1(O10), .O2(O20), .O3(O30), .O4(O40), .O5(O50),
    .O6(O60), .O7(O70));
  or or_1 (O0, O03, O02, O01, O00);
  or or_2 (O4, O43, O42, O41, O40);
  _2Bit_Decoder _2bit_decoder_2 (.S0(S2), .S1(S3), .EN(RD), .O0(RD0), .O1(RD1), .O2(RD2), .O3(RD3));
  _4x8Ram _4x8ram_2 (
    .I0(I0_t), .I1(I1_t), .I2(I2_t), .I3(I3_t), .I4(I4_t), .I5(I5_t), .I6(I6_t), .I7(I7_t), .CLK(CLK),
    .S0(S0), .S1(S1), .WR(WR1), .RD(RD1), .O0(O01), .O1(O11), .O2(O21), .O3(O31), .O4(O41), .O5(O51),
    .O6(O61), .O7(O71));
  or or_3 (O1, O13, O12, O11, O10);
  or or_4 (O5, O53, O52, O51, O50);
  _4x8Ram _4x8ram_3 (
    .I0(I0_t), .I1(I1_t), .I2(I2_t), .I3(I3_t), .I4(I4_t), .I5(I5_t), .I6(I6_t), .I7(I7_t), .CLK(CLK),
    .S0(S0), .S1(S1), .WR(WR2), .RD(RD2), .O0(O02), .O1(O12), .O2(O22), .O3(O32), .O4(O42), .O5(O52),
    .O6(O62), .O7(O72));
  or or_5 (O2, O23, O22, O21, O20);
  or or_6 (O6, O63, O62, O61, O60);
  _4x8Ram _4x8ram_4 (
    .I0(I0_t), .I1(I1_t), .I2(I2_t), .I3(I3_t), .I4(I4_t), .I5(I5_t), .I6(I6_t), .I7(I7_t), .CLK(CLK),
    .S0(S0), .S1(S1), .WR(WR3), .RD(RD3), .O0(O03), .O1(O13), .O2(O23), .O3(O33), .O4(O43), .O5(O53),
    .O6(O63), .O7(O73));
  or or_7 (O3, O33, O32, O31, O30);
  or or_8 (O7, O73, O72, O71, O70);

  // Other names for the same wires on the sheet: I_0 = I0; I_1 = I1; I_2 = I2; I_3 = I3; I_4 = I4; I_5 = I5; I_6 = I6;
  //   I_7 = I7
endmodule
