// Digital circuit 2Bit_Decoder.dig as structural Verilog
module _2Bit_Decoder (
  input  S0,
  input  S1,
  input  EN,
  output O0,
  output O1,
  output O2,
  output O3
);

  wire and_1_out, and_2_out, not_1_out, not_2_out;

  and and_1 (and_1_out, S1, EN);
  and and_2 (and_2_out, S0, EN);
  not not_1 (not_1_out, and_1_out);
  not not_2 (not_2_out, and_2_out);
  and and_3 (O0, not_1_out, EN, not_2_out);
  and and_4 (O1, not_1_out, and_2_out);
  and and_5 (O2, and_1_out, not_2_out);
  and and_6 (O3, and_1_out, and_2_out);
endmodule
