// Digital circuit 4Bit_Decoder.dig as structural Verilog
module _4Bit_Decoder (
  input  S3,
  input  S2,
  input  S1,
  input  S0,
  input  EN,
  output O0,
  output O1,
  output O2,
  output O3,
  output O4,
  output O5,
  output O6,
  output O7,
  output _08,
  output O9,
  output O10,
  output O11,
  output O12,
  output O13,
  output O14,
  output O15
);

  wire and_1_out, and_2_out, and_3_out, and_4_out, not_1_out, not_2_out, not_3_out, not_4_out;

  and and_1 (and_1_out, S3, EN);
  not not_1 (not_1_out, and_1_out);
  and and_2 (and_2_out, S2, EN);
  not not_2 (not_2_out, and_2_out);
  and and_3 (and_3_out, S1, EN);
  not not_3 (not_3_out, and_3_out);
  not not_4 (not_4_out, and_4_out);
  and and_4 (and_4_out, S0, EN);
  and and_5 (O0, not_1_out, not_2_out, EN, not_3_out, not_4_out);
  and and_6 (O1, not_1_out, not_2_out, not_3_out, and_4_out);
  and and_7 (O2, not_1_out, not_2_out, and_3_out, not_4_out);
  and and_8 (O3, not_1_out, not_2_out, and_3_out, and_4_out);
  and and_9 (O4, not_1_out, and_2_out, not_3_out, not_4_out);
  and and_10 (O5, not_1_out, and_2_out, not_3_out, and_4_out);
  and and_11 (O6, not_1_out, and_2_out, and_3_out, not_4_out);
  and and_12 (O7, not_1_out, and_2_out, and_3_out, and_4_out);
  and and_13 (_08, and_1_out, not_2_out, not_3_out, not_4_out);
  and and_14 (O9, and_1_out, not_2_out, not_3_out, and_4_out);
  and and_15 (O10, and_1_out, not_2_out, and_3_out, not_4_out);
  and and_16 (O11, and_1_out, not_2_out, and_3_out, and_4_out);
  and and_17 (O12, and_1_out, and_2_out, not_3_out, not_4_out);
  and and_18 (O13, and_1_out, and_2_out, not_3_out, and_4_out);
  and and_19 (O14, and_1_out, and_2_out, and_3_out, not_4_out);
  and and_20 (O15, and_1_out, and_2_out, and_3_out, and_4_out);
endmodule
