// Digital circuit 4bit_encoder.dig as structural Verilog
module _4bit_encoder (
  input  S0,
  input  S1,
  input  S2,
  input  S3,
  output P0,
  output P1,
  output DV
);

  or or_1 (DV, S0, S1, S2, S3);
  or or_2 (P1, S2, S3);
  or or_3 (P0, S1, S3);
endmodule
