// Digital circuit 6_ringcounter.dig as structural Verilog
module _6_ringcounter (
  input  EN,
  input  CLK,
  output S0,
  output S1,
  output S2,
  output S3,
  output S4,
  output S5
);

  wire nor_1_out;

  Register R0 (.D(nor_1_out), .C(CLK), .en(EN), .Q(S0));
  nor nor_1 (nor_1_out, S0, S1, S1, S2, S2, S3, S3, S4);
  Register R1 (.D(S0), .C(CLK), .en(EN), .Q(S1));
  Register R2 (.D(S1), .C(CLK), .en(EN), .Q(S2));
  Register R3 (.D(S2), .C(CLK), .en(EN), .Q(S3));
  Register R4 (.D(S3), .C(CLK), .en(EN), .Q(S4));
  Register R5 (.D(S4), .C(CLK), .en(EN), .Q(S5));
endmodule
