// Digital circuit 8Bit_reg.dig as structural Verilog
module _8Bit_reg (
  input  I0,
  input  I1,
  input  I2,
  input  I3,
  input  I4,
  input  I5,
  input  I6,
  input  I7,
  input  Clock,
  input  WR,
  input  RD,
  output O0,
  output O1,
  output O2,
  output O3,
  output O4,
  output O5,
  output O6,
  output O7
);

  wire register_1_q, register_2_q, register_3_q, register_4_q, register_5_q, register_6_q, register_7_q,
       register_8_q;

  Register register_1 (.D(I0), .C(Clock), .en(WR), .Q(register_1_q));
  Register register_2 (.D(I1), .C(Clock), .en(WR), .Q(register_2_q));
  Register register_3 (.D(I2), .C(Clock), .en(WR), .Q(register_3_q));
  Register register_4 (.D(I3), .C(Clock), .en(WR), .Q(register_4_q));
  Register register_5 (.D(I4), .C(Clock), .en(WR), .Q(register_5_q));
  Register register_6 (.D(I5), .C(Clock), .en(WR), .Q(register_6_q));
  Register register_7 (.D(I6), .C(Clock), .en(WR), .Q(register_7_q));
  Register register_8 (.D(I7), .C(Clock), .en(WR), .Q(register_8_q));
  and and_1 (O0, RD, register_1_q);
  and and_2 (O1, RD, register_2_q);
  and and_3 (O2, RD, register_3_q);
  and and_4 (O3, RD, register_4_q);
  and and_5 (O4, RD, register_5_q);
  and and_6 (O5, RD, register_6_q);
  and and_7 (O6, RD, register_7_q);
  and and_8 (O7, RD, register_8_q);
endmodule
