// Digital circuit 8_bit_sub.dig as structural Verilog
module _8_bit_sub (
  input  A0,
  input  B0,
  input  B1,
  input  B2,
  input  B3,
  input  B4,
  input  B5,
  input  B6,
  input  B7,
  input  A1,
  input  A2,
  input  A3,
  input  A4,
  input  A5,
  input  A6,
  input  A7,
  output out_17,
  output out_18,
  output out_19,
  output out_20,
  output out_21,
  output out_22,
  output out_23,
  output out_24,
  output out_25
);

  wire _4bit_adder_1_p14, not_1_out, not_2_out, not_3_out, not_4_out, not_5_out, not_6_out, not_7_out,
       not_8_out;

  not not_1 (not_1_out, B0);
  not not_2 (not_2_out, B1);
  not not_3 (not_3_out, B2);
  not not_4 (not_4_out, B3);
  not not_5 (not_5_out, B4);
  not not_6 (not_6_out, B5);
  not not_7 (not_7_out, B6);
  not not_8 (not_8_out, B7);
  // _4bit_adder _4bit_adder_1: pin names not known; wires that end beside it: A0, A1, A2, A3, not_1_out, not_2_out, not_3_out, not_4_out, 1'b1, out_17, out_18, out_19, out_20, _4bit_adder_1_p14
  // _4bit_adder _4bit_adder_2: pin names not known; wires that end beside it: A4, A5, A6, A7, not_5_out, not_6_out, not_7_out, not_8_out, _4bit_adder_1_p14, out_22, out_23, out_24, out_25, out_21
endmodule
