// Digital circuit Controller.dig as structural Verilog
module Controller (
  input  CLK,
  input  [3:0] OP,
  input  EN,
  output C_P,
  output E_P,
  output L_M,
  output CE,
  output R_S,
  output L_I,
  output E_I,
  output L_A,
  output E_A,
  output S_U,
  output E_U,
  output L_B,
  output L_O
);

  wire _6_ringcounter_1_s3, _6_ringcounter_1_s4, _6_ringcounter_1_s5, A, and_1_out, and_2_out, and_4_out,
       and_5_out, and_6_out, and_7_out, and_8_out, and_9_out, and_10_out, and_11_out, AOS, LOS,
       opcode_decoder_1_lda, opcode_decoder_1_out, opcode_decoder_1_str, S;

  or or_1 (AOS, S, A);
  Opcode_Decoder opcode_decoder_1 (
    .D(OP[0]), .C(OP[1]), .B(OP[2]), .A(OP[3]), .LDA(opcode_decoder_1_lda), .ADD(A), .SUB(S),
    .OUT(opcode_decoder_1_out), .STR(opcode_decoder_1_str));  // open: HLT
  or or_2 (LOS, opcode_decoder_1_lda, opcode_decoder_1_str);
  and and_1 (and_1_out, _6_ringcounter_1_s3, LOS);
  or or_3 (L_M, and_2_out, and_1_out, E_P);
  and and_2 (and_2_out, _6_ringcounter_1_s3, AOS);
  and and_3 (R_S, _6_ringcounter_1_s4, opcode_decoder_1_str);
  and and_4 (and_4_out, opcode_decoder_1_lda, _6_ringcounter_1_s4);
  or or_4 (CE, and_5_out, and_4_out, L_I);
  and and_5 (and_5_out, _6_ringcounter_1_s4, AOS);
  and and_6 (and_6_out, _6_ringcounter_1_s3, LOS);
  or or_5 (E_I, and_7_out, and_6_out);
  and and_7 (and_7_out, _6_ringcounter_1_s3, AOS);
  and and_8 (and_8_out, opcode_decoder_1_lda, _6_ringcounter_1_s4);
  or or_6 (L_A, and_9_out, and_8_out);
  and and_9 (and_9_out, AOS, _6_ringcounter_1_s5);
  _6_ringcounter _6_ringcounter_1 (
    .EN(EN), .CLK(CLK), .S0(E_P), .S1(C_P), .S2(L_I), .S3(_6_ringcounter_1_s3), .S4(_6_ringcounter_1_s4),
    .S5(_6_ringcounter_1_s5));
  and and_10 (and_10_out, _6_ringcounter_1_s4, opcode_decoder_1_str);
  and and_11 (and_11_out, _6_ringcounter_1_s3, opcode_decoder_1_out);
  or or_7 (E_A, and_11_out, and_10_out);
  and and_12 (S_U, _6_ringcounter_1_s5, S);
  and and_13 (E_U, _6_ringcounter_1_s5, AOS);
  and and_14 (L_B, AOS, _6_ringcounter_1_s4);
  and and_15 (L_O, opcode_decoder_1_out, _6_ringcounter_1_s3);
endmodule
