// Digital circuit Opcode Decoder.dig as structural Verilog
module Opcode_Decoder (
  input  D,
  input  C,
  input  B,
  input  A,
  output LDA,
  output ADD,
  output SUB,
  output OUT,
  output HLT,
  output STR
);

  wire not_1_out, not_2_out, not_3_out, not_4_out;

  not not_1 (not_1_out, A);
  not not_2 (not_2_out, B);
  not not_3 (not_3_out, C);
  not not_4 (not_4_out, D);
  and and_1 (LDA, not_1_out, not_2_out, not_3_out, not_4_out);
  and and_2 (ADD, not_1_out, not_2_out, not_3_out, D);
  and and_3 (SUB, not_1_out, not_2_out, C, not_4_out);
  and and_4 (OUT, A, B, C, not_4_out);
  and and_5 (STR, A, B, not_3_out, D);
  and and_6 (HLT, A, B, C, D);
endmodule
