// Digital circuit add-sub.dig as structural Verilog
module add_sub (
  input  [7:0] A,
  input  [7:0] B,
  input  A_s,
  output [7:0] S,
  output OV,
  output TS,
  output Cout
);

  wire B0, B1, B2, B3, B4, B5, B6, B7, full_adder_1_cout, full_adder_2_cout, full_adder_3_cout,
       full_adder_5_cout, full_adder_6_cout, full_adder_7_cout, HC;
  wire [7:0] not_1_out;

  assign not_1_out = ~B;  // Not not_1, 8 bits wide
  Multiplexer #(.Bits(8)) multiplexer_1 (.sel(A_s), .in_0(B), .in_1(not_1_out), .out({B7, B6, B5, B4, B3, B2, B1, B0}));
  full_adder full_adder_1 (.A(A[0]), .B(B0), .Cin(A_s), .S(S[0]), .Cout(full_adder_1_cout));
  full_adder full_adder_2 (.A(A[1]), .B(B1), .Cin(full_adder_1_cout), .S(S[1]), .Cout(full_adder_2_cout));
  full_adder full_adder_3 (.A(A[2]), .B(B2), .Cin(full_adder_2_cout), .S(S[2]), .Cout(full_adder_3_cout));
  full_adder full_adder_4 (.A(A[3]), .B(B3), .Cin(full_adder_3_cout), .S(S[3]), .Cout(HC));
  full_adder full_adder_5 (.A(A[4]), .B(B4), .Cin(HC), .S(S[4]), .Cout(full_adder_5_cout));
  full_adder full_adder_6 (.A(A[5]), .B(B5), .Cin(full_adder_5_cout), .S(S[5]), .Cout(full_adder_6_cout));
  full_adder full_adder_7 (.A(A[6]), .B(B6), .Cin(full_adder_6_cout), .S(S[6]), .Cout(full_adder_7_cout));
  full_adder full_adder_8 (.A(A[7]), .B(B7), .Cin(full_adder_7_cout), .S(S[7]), .Cout(Cout));
  xor xor_1 (OV, full_adder_7_cout, Cout);
  xor xor_2 (TS, OV, S[7]);

  // Other names for the same wires on the sheet: Cin = A_s
endmodule
