// Digital circuit full_adder.dig as structural Verilog
module full_adder (
  input  A,
  input  B,
  input  Cin,
  output S,
  output Cout
);

  wire half_adder_1_c, half_adder_1_s, half_adder_2_c;

  half_adder half_adder_1 (.A(B), .B(Cin), .S(half_adder_1_s), .C(half_adder_1_c));
  half_adder half_adder_2 (.A(A), .B(half_adder_1_s), .S(S), .C(half_adder_2_c));
  or or_1 (Cout, half_adder_2_c, half_adder_1_c);
endmodule
